# Fritzing sketch Schema_rj45 (saved by Fritzing 0.9.3b)
circuit board: 10cm x 6cm
breadboards: 1

parts:
  TP-UART = double row female pin header, 10 pins [form="♀ (female)"]
  J1 = male pin header, 2 pins [form="♂ (male)"]
  U2 = LM 358 Dual Op-Amp [package="DIP8 [THT]"]
  U3 = LM 358 Dual Op-Amp [package="DIP8 [THT]"]
  R1 = Resistor [tolerance=±1% resistance=100k package="0603 [SMD]"]
  R2 = Resistor [tolerance=±1% resistance=150k package="0603 [SMD]"]
  R6 = Resistor [tolerance=±1% resistance=1M package="0603 [SMD]"]
  R5 = Resistor [tolerance=±1% resistance=0 package="0603 [SMD]"]
  R8 = Resistor [tolerance=±1% resistance=1M package="0603 [SMD]"]
  R7 = Resistor [tolerance=±1% resistance=0 package="0603 [SMD]"]
  C5 = Ceramic Capacitor [capacitance=10pF package="0603 [SMD, multilayer]"]
  C7 = Ceramic Capacitor [capacitance=10pF package="0603 [SMD, multilayer]"]
  C8 = Ceramic Capacitor [capacitance=10pF package="0603 [SMD, multilayer]"]
  J4 = screw terminal, 3 pins
  C2 = Ceramic Capacitor [capacitance=100nF package="0603 [SMD, multilayer]"]
  R4 = Resistor [tolerance=±1% resistance=1M package="0603 [SMD]"]
  Nucleo = Nucleo-32 STM32L432KC
  J8 = screw terminal, 3 pins
  R25 = Resistor [tolerance=±1% resistance=4.7k package="0603 [SMD]"]
  C1 = Electrolytic Capacitor [capacitance=10µF package="100 mil [THT, electrolytic]"]
  R29 = Resistor [tolerance=±1% resistance=100k package="0603 [SMD]"]
  R26 = Resistor [tolerance=±1% resistance=100k package="0603 [SMD]"]
  R28 = Resistor [tolerance=±1% resistance=100k package="0603 [SMD]"]
  R27 = Resistor [tolerance=±1% resistance=100k package="0603 [SMD]"]
  U4 = RJ45 Jack [package=rj45-8]
  C6 = Ceramic Capacitor [capacitance=10pF package="0603 [SMD, multilayer]"]
  R3 = Resistor [tolerance=±1% resistance=0 package="0603 [SMD]"]
  C4 = Ceramic Capacitor [capacitance=100nF package="0603 [SMD, multilayer]"]
  C3 = Ceramic Capacitor [capacitance=100nF package="0603 [SMD, multilayer]"]
  U5 = RJ45 Jack [package=rj45-8]
  R21 = Resistor [tolerance=±1% resistance=0 package="0603 [SMD]"]
  R17 = Resistor [tolerance=±1% resistance=0 package="0603 [SMD]"]
  R11 = Resistor [tolerance=±1% resistance=4.7k package="0603 [SMD]"]
  C9 = Ceramic Capacitor [capacitance=10pF package="0603 [SMD, multilayer]"]
  R12 = Resistor [tolerance=±1% resistance=4.7k package="0603 [SMD]"]
  C10 = Ceramic Capacitor [capacitance=10pF package="0603 [SMD, multilayer]"]
  R15 = Resistor [tolerance=±1% resistance=4.7k package="0603 [SMD]"]
  C11 = Ceramic Capacitor [capacitance=10pF package="0603 [SMD, multilayer]"]
  R10 = Resistor [tolerance=±1% resistance=0 package="0603 [SMD]"]
  R9 = Resistor [tolerance=±1% resistance=4.7k package="0603 [SMD]"]
  R14 = Resistor [tolerance=±1% resistance=0 package="0603 [SMD]"]
  R13 = Resistor [tolerance=±1% resistance=4.7k package="0603 [SMD]"]
  R16 = Resistor [tolerance=±1% resistance=4.7k package="0603 [SMD]"]
  R18 = Resistor [tolerance=±1% resistance=4.7k package="0603 [SMD]"]
  R19 = Resistor [tolerance=±1% resistance=0 package="0603 [SMD]"]
  R20 = Resistor [tolerance=±1% resistance=4.7k package="0603 [SMD]"]
  R23 = Resistor [tolerance=±1% resistance=0 package="0603 [SMD]"]
  R22 = Resistor [tolerance=±1% resistance=4.7k package="0603 [SMD]"]
  R24 = Resistor [tolerance=±1% resistance=4.7k package="0603 [SMD]"]
  R26_2 = Resistor [tolerance=±1% resistance=4.7k package="0603 [SMD]"]
  C12 = Ceramic Capacitor [capacitance=10pF package="0603 [SMD, multilayer]"]
  C13 = Ceramic Capacitor [capacitance=10pF package="0603 [SMD, multilayer]"]
  C14 = Ceramic Capacitor [capacitance=10pF package="0603 [SMD, multilayer]"]

nets:
  N1: TP-UART.pin1, J1.pin2
  N2: TP-UART.pin2, Nucleo.D0/RX
  N3: TP-UART.pin4, Nucleo.D1/TX
  GND: TP-UART.pin5, U2.connector3, U3.connector3, R1.Pin_0, R6.Pin_0, R8.Pin_0, C2.0, R4.Pin_0, Nucleo.GND, C1.-, R28.Pin_0, R27.Pin_0, U4.1, C4.0, C3.0, U5.8, R11.Pin_1, C9.1, R12.Pin_1, C10.1, R15.Pin_1, C11.1, C12.0, C13.0, C14.0
  5V: J1.pin1, U2.connector7, U3.connector7, J4.pin2, C2.1, Nucleo.5V, R25.Pin_0, C1.+, C4.1, C3.1, U5.7, R9.Pin_1, R13.Pin_1, R16.Pin_1, R18.Pin_1, R20.Pin_1, R22.Pin_1, R24.Pin_1, R26_2.Pin_1
  N4: U2.connector0, R5.Pin_1, C7.1, Nucleo.A4
  N5: U2.connector1, R6.Pin_1, R5.Pin_0, C7.0
  N6: U2.connector2, U4.7
  N7: U2.connector4, U4.6
  N8: U2.connector5, R8.Pin_1, R7.Pin_0, C8.0
  N9: U2.connector6, R7.Pin_1, C8.1, Nucleo.A5
  N10: U3.connector0, R2.Pin_0, C5.0, Nucleo.A2
  N11: U3.connector1, R1.Pin_1, R2.Pin_1, C5.1
  N12: U3.connector2, U4.3
  N13: U3.connector4, U4.2
  N14: U3.connector5, R4.Pin_1, C6.0, R3.Pin_0
  N15: U3.connector6, Nucleo.A3, C6.1, R3.Pin_1
  N16: J4.pin1, R26.Pin_1
  N17: J4.pin3, R29.Pin_1, U4.8
  N18: Nucleo.D2, R11.Pin_0, C9.0, R10.Pin_1
  N19: Nucleo.D3, R12.Pin_0, C10.0, R14.Pin_1
  N20: Nucleo.D4, R17.Pin_1, R15.Pin_0, C11.0
  N21: Nucleo.D5, R19.Pin_1, C12.1
  N22: Nucleo.D6, R21.Pin_1, C13.1
  N23: Nucleo.D7, R23.Pin_1, C14.1
  N24: Nucleo.D8, J8.pin1, R24.Pin_0
  N25: Nucleo.D9, J8.pin2, R26_2.Pin_0
  N26: Nucleo.D10, J8.pin3, R25.Pin_1
  N27: Nucleo.A7, U4.5
  N28: Nucleo.A6, U4.4
  N29: Nucleo.A1, R29.Pin_0, R28.Pin_1
  N30: Nucleo.A0, R26.Pin_0, R27.Pin_1
  N31: U5.1, R10.Pin_0, R9.Pin_0
  N32: U5.2, R14.Pin_0, R13.Pin_0
  N33: U5.3, R17.Pin_0, R16.Pin_0
  N34: U5.4, R18.Pin_0, R19.Pin_0
  N35: U5.5, R21.Pin_0, R20.Pin_0
  N36: U5.6, R23.Pin_0, R22.Pin_0

notes:
  Nucleo-KNX V1.0
  By Fabien Proriol

custom parts:
  Nucleo-32 STM32L432KC: STMicroelectronics STM32 Nucleo Development Boards provide an affordable and flexible way for users to try out new ideas and build prototypes with any STM32 microcontroller line, choosing from the various combinations of performance, power consumption, and features.
